# Fritzing sketch Projet Voiture (saved by Fritzing 0.9.2b)
breadboards: 2

parts:
  S2 = H-Bridge with L298N
  M1 = DC Motor  # not connected
  M2 = DC Motor
  M3 = DC Motor
  M4 = DC Motor
  Composant1 = Arduino Uno (Rev3)
  U1 = POT [package=pot_alpha_rv16af-20]
  VCC1 = Battery block 9V

nets:
  N1: S2.12V, VCC1.+
  N2: S2.GND, VCC1.-
  N3: S2.ENA, Composant1.D6_PWM
  N4: S2.IN1, Composant1.D5_PWM
  N5: S2.IN2, Composant1.D7
  N6: S2.IN3, Composant1.D4
  N7: S2.IN4, Composant1.D2
  N8: S2.ENB, Composant1.D3_PWM
  N9: S2.M1-01, M2.pin_1, M4.pin_1
  N10: S2.M1-02, M2.pin_2, M4.pin_2
  N11: S2.M2-01, M3.pin_2
  N12: S2.M2-02, M3.pin_1
  N13: Composant1.A0, U1.A
  N14: Composant1.5V, U1.E
  N15: Composant1.GND, U1.S

notes:
  Avant voiture
  envoi du courant vers +:
  - OUT1 et OUT4
  Gauche
  envoi vers:
  - OUT 1 et OUT3
  derrière voiture
  envoi vers :
  - OUT2 et OUT3
  Droite
  envoi vers:
  - OUT 4 et OUT2

custom parts:
  H-Bridge with L298N: h-bridge
